// Logisim project banco_registradores.circ as structural Verilog: 1 circuit, main circuit main
module main (
);

  wire demultiplexer_1_out0, demultiplexer_1_out1, demultiplexer_1_out2, demultiplexer_1_out3,
       demultiplexer_1_out4, demultiplexer_1_out5, demultiplexer_1_out6, demultiplexer_1_out7,
       demultiplexer_1_out8, demultiplexer_1_out9, demultiplexer_1_out10, demultiplexer_1_out11,
       demultiplexer_1_out12, demultiplexer_1_out13, demultiplexer_1_out14, demultiplexer_1_out15,
       demultiplexer_1_out16, demultiplexer_1_out17, demultiplexer_1_out18, demultiplexer_1_out19,
       demultiplexer_1_out20, demultiplexer_1_out21, demultiplexer_1_out22, demultiplexer_1_out23,
       demultiplexer_1_out24, demultiplexer_1_out25, demultiplexer_1_out26, demultiplexer_1_out27,
       demultiplexer_1_out28, demultiplexer_1_out29, demultiplexer_1_out30, demultiplexer_1_out31;
  wire [31:0] clock_1_out, register_17_q, register_18_q, register_19_q, register_20_q, register_21_q,
       register_22_q, register_23_q, register_25_q, register_26_q, register_27_q, register_29_p1,
       register_29_p4, register_29_p6, register_30_q, register_31_p4, register_31_p6, register_32_q,
       undriven, undriven_2, undriven_3, undriven_4, undriven_5, undriven_6, undriven_7, undriven_8,
       undriven_9, undriven_10, undriven_11, undriven_12, undriven_13, undriven_14, undriven_15, undriven_16,
       undriven_17, undriven_18;

  Demultiplexer #(.enable("true"), .select(5)) demultiplexer_1 (
    .out0(demultiplexer_1_out0), .out1(demultiplexer_1_out1), .out2(demultiplexer_1_out2),
    .out3(demultiplexer_1_out3), .out4(demultiplexer_1_out4), .out5(demultiplexer_1_out5),
    .out6(demultiplexer_1_out6), .out7(demultiplexer_1_out7), .out8(demultiplexer_1_out8),
    .out9(demultiplexer_1_out9), .out10(demultiplexer_1_out10), .out11(demultiplexer_1_out11),
    .out12(demultiplexer_1_out12), .out13(demultiplexer_1_out13), .out14(demultiplexer_1_out14),
    .out15(demultiplexer_1_out15), .out16(demultiplexer_1_out16), .out17(demultiplexer_1_out17),
    .out18(demultiplexer_1_out18), .out19(demultiplexer_1_out19), .out20(demultiplexer_1_out20),
    .out21(demultiplexer_1_out21), .out22(demultiplexer_1_out22), .out23(demultiplexer_1_out23),
    .out24(demultiplexer_1_out24), .out25(demultiplexer_1_out25), .out26(demultiplexer_1_out26),
    .out27(demultiplexer_1_out27), .out28(demultiplexer_1_out28), .out29(demultiplexer_1_out29),
    .out30(demultiplexer_1_out30), .out31(demultiplexer_1_out31));  // open: in, sel, en
  Clock clock_1 (.out(clock_1_out[0]));
  Register #(.width(32)) register_1 (
    .D(clock_1_out), .en(demultiplexer_1_out2), .clk(demultiplexer_1_out4), .Q(clock_1_out),
    .clr(demultiplexer_1_out6));
  Register #(.width(32)) register_2 (
    .D(clock_1_out), .en(demultiplexer_1_out10), .clk(demultiplexer_1_out12), .Q(clock_1_out),
    .clr(demultiplexer_1_out14));
  Register #(.width(32)) register_3 (
    .D(clock_1_out), .en(demultiplexer_1_out18), .clk(demultiplexer_1_out20), .Q(clock_1_out),
    .clr(demultiplexer_1_out22));
  Register #(.width(32)) register_4 (
    .D(clock_1_out), .en(demultiplexer_1_out26), .clk(demultiplexer_1_out28), .Q(clock_1_out),
    .clr(demultiplexer_1_out30));
  Register #(.width(32)) register_5 (
    .D(clock_1_out), .en(demultiplexer_1_out2), .clk(demultiplexer_1_out4), .Q(clock_1_out),
    .clr(demultiplexer_1_out6));
  Register #(.width(32)) register_6 (
    .D(clock_1_out), .clk(demultiplexer_1_out4), .Q(clock_1_out), .clr(demultiplexer_1_out6));  // open: en
  Register #(.width(32)) register_7 (
    .D(clock_1_out), .en(demultiplexer_1_out10), .clk(demultiplexer_1_out12), .Q(clock_1_out),
    .clr(demultiplexer_1_out14));
  Register #(.width(32)) register_8 (
    .D(clock_1_out), .clk(demultiplexer_1_out12), .Q(clock_1_out), .clr(demultiplexer_1_out14));  // open: en
  Register #(.width(32)) register_9 (
    .D(clock_1_out), .en(demultiplexer_1_out18), .clk(demultiplexer_1_out20), .Q(clock_1_out),
    .clr(demultiplexer_1_out22));
  Register #(.width(32)) register_10 (
    .D(clock_1_out), .clk(demultiplexer_1_out20), .Q(clock_1_out), .clr(demultiplexer_1_out22));  // open: en
  Register #(.width(32)) register_11 (
    .D(clock_1_out), .en(demultiplexer_1_out26), .clk(demultiplexer_1_out28), .Q(clock_1_out),
    .clr(demultiplexer_1_out30));
  Register #(.width(32)) register_12 (
    .D(clock_1_out), .clk(demultiplexer_1_out28), .Q(clock_1_out), .clr(demultiplexer_1_out30));  // open: en
  Register #(.width(32)) register_13 (
    .D(clock_1_out), .clk(demultiplexer_1_out4), .Q(clock_1_out), .clr(demultiplexer_1_out6));  // open: en
  Register #(.width(32)) register_14 (
    .D(clock_1_out), .clk(demultiplexer_1_out12), .Q(clock_1_out), .clr(demultiplexer_1_out14));  // open: en
  Register #(.width(32)) register_15 (
    .D(clock_1_out), .clk(demultiplexer_1_out20), .Q(clock_1_out), .clr(demultiplexer_1_out22));  // open: en
  Register #(.width(32)) register_16 (
    .D(clock_1_out), .clk(demultiplexer_1_out28), .Q(clock_1_out), .clr(demultiplexer_1_out30));  // open: en
  Register #(.width(32)) register_17 (
    .D(register_29_p1), .en(demultiplexer_1_out4), .Q(register_17_q), .clk(clock_1_out[0]));  // open: clr
  Register #(.width(32)) register_18 (
    .D(register_29_p1), .en(demultiplexer_1_out12), .Q(register_18_q), .clk(clock_1_out[0]));  // open: clr
  Register #(.width(32)) register_19 (
    .D(register_29_p1), .en(demultiplexer_1_out20), .Q(register_19_q), .clk(clock_1_out[0]));  // open: clr
  Register #(.width(32)) register_20 (
    .D(register_29_p1), .en(demultiplexer_1_out28), .Q(register_20_q), .clk(clock_1_out[0]));  // open: clr
  Register #(.width(32)) register_21 (
    .D(register_29_p1), .en(demultiplexer_1_out5), .Q(register_21_q), .clk(clock_1_out[0]));  // open: clr
  Register #(.width(32)) register_22 (.D(clock_1_out), .Q(register_22_q), .clr(demultiplexer_1_out7));  // open: en, clk
  Register #(.width(32)) register_23 (
    .D(register_29_p1), .en(demultiplexer_1_out13), .Q(register_23_q), .clk(clock_1_out[0]));  // open: clr
  Register #(.width(32)) register_24 (.D(clock_1_out), .clr(demultiplexer_1_out15));  // open: en, clk, Q
  Register #(.width(32)) register_25 (
    .D(register_29_p1), .en(demultiplexer_1_out21), .Q(register_25_q), .clk(clock_1_out[0]));  // open: clr
  Register #(.width(32)) register_26 (
    .D(clock_1_out), .Q(register_26_q), .clr(demultiplexer_1_out23));  // open: en, clk
  Register #(.width(32)) register_27 (
    .D(register_29_p1), .en(demultiplexer_1_out29), .Q(register_27_q), .clk(clock_1_out[0]));  // open: clr
  Register #(.width(32)) register_28 (.D(clock_1_out), .clr(demultiplexer_1_out31));  // open: en, clk, Q
  // Register #(.width(32)) register_29: pin names not known; wires that end beside it: register_29_p1, demultiplexer_1_out7, clock_1_out, register_29_p4, register_22_q, register_29_p6, register_29_p6
  Register #(.width(32)) register_30 (
    .D(register_29_p1), .en(demultiplexer_1_out15), .Q(register_30_q), .clk(clock_1_out[0]));  // open: clr
  // Register #(.width(32)) register_31: pin names not known; wires that end beside it: register_29_p1, demultiplexer_1_out23, clock_1_out, register_31_p4, register_26_q, register_31_p6, register_20_q
  Register #(.width(32)) register_32 (
    .D(register_29_p1), .en(demultiplexer_1_out31), .Q(register_32_q), .clk(clock_1_out[0]));  // open: clr
  Multiplexer #(.enable("true"), .select(5), .width(32)) multiplexer_1 (
    .in0(undriven), .in1(undriven_3), .in2(undriven_5), .in3(undriven_7), .in4(register_17_q),
    .in5(register_21_q), .in6(undriven_9), .in7(register_29_p4), .in8(undriven_12), .in9(undriven_13),
    .in10(register_29_p6), .in11(undriven_15), .in12(register_18_q), .in13(register_23_q),
    .in14(undriven_18), .in15(register_30_q), .in16(undriven_2), .in17(undriven_4), .in18(undriven_6),
    .in19(undriven_8), .in20(register_19_q), .in21(register_25_q), .in22(undriven_11), .in23(register_31_p4),
    .in24(undriven_14), .in25(register_31_p6), .in26(undriven_16), .in27(undriven_17), .in28(register_20_q),
    .in29(register_27_q), .in30(undriven_10), .in31(register_32_q));  // open: out, sel, en
  // Pins of 1 and 32 bits meet at clock_1_out
endmodule
