// Logisim project cpu-novo.circ as structural Verilog
module registers (
  input  [31:0] write_data,
  input  [4:0] read_reg1,
  input  [4:0] write_reg,
  input  [4:0] read_reg2,
  output [31:0] read_data1,
  output [31:0] read_data2
);

  wire clock_1_out, demultiplexer_1_out0, demultiplexer_1_out1, demultiplexer_1_out2, demultiplexer_1_out3,
       demultiplexer_1_out4, demultiplexer_1_out5, demultiplexer_1_out6, demultiplexer_1_out7,
       demultiplexer_1_out8, demultiplexer_1_out9, demultiplexer_1_out10, demultiplexer_1_out11,
       demultiplexer_1_out12, demultiplexer_1_out13, demultiplexer_1_out14, demultiplexer_1_out15,
       demultiplexer_1_out16, demultiplexer_1_out17, demultiplexer_1_out18, demultiplexer_1_out19,
       demultiplexer_1_out20, demultiplexer_1_out21, demultiplexer_1_out22, demultiplexer_1_out23,
       demultiplexer_1_out24, demultiplexer_1_out25, demultiplexer_1_out26, demultiplexer_1_out27,
       demultiplexer_1_out28, demultiplexer_1_out29, demultiplexer_1_out30, demultiplexer_1_out31;
  wire [31:0] register_1_q, register_2_q, register_3_q, register_4_q, register_5_q, register_6_q,
       register_7_q, register_8_q, register_9_q, register_10_q, register_11_q, register_12_q, register_13_q,
       register_14_q, register_15_q, register_16_q, register_17_q, register_18_q, register_19_q,
       register_20_q, register_21_q, register_22_q, register_23_q, register_24_q, register_25_q,
       register_26_q, register_27_q, register_28_q, register_29_q, register_30_q, register_31_q,
       register_32_q;

  Demultiplexer #(.select(5)) demultiplexer_1 (
    .out0(demultiplexer_1_out0), .out1(demultiplexer_1_out1), .out2(demultiplexer_1_out2),
    .out3(demultiplexer_1_out3), .out4(demultiplexer_1_out4), .out5(demultiplexer_1_out5),
    .out6(demultiplexer_1_out6), .out7(demultiplexer_1_out7), .out8(demultiplexer_1_out8),
    .out9(demultiplexer_1_out9), .out10(demultiplexer_1_out10), .out11(demultiplexer_1_out11),
    .out12(demultiplexer_1_out12), .out13(demultiplexer_1_out13), .out14(demultiplexer_1_out14),
    .out15(demultiplexer_1_out15), .out16(demultiplexer_1_out16), .out17(demultiplexer_1_out17),
    .out18(demultiplexer_1_out18), .out19(demultiplexer_1_out19), .out20(demultiplexer_1_out20),
    .out21(demultiplexer_1_out21), .out22(demultiplexer_1_out22), .out23(demultiplexer_1_out23),
    .out24(demultiplexer_1_out24), .out25(demultiplexer_1_out25), .out26(demultiplexer_1_out26),
    .out27(demultiplexer_1_out27), .out28(demultiplexer_1_out28), .out29(demultiplexer_1_out29),
    .out30(demultiplexer_1_out30), .out31(demultiplexer_1_out31), .in(1'b1), .sel(write_reg));
  Clock clock_1 (.out(clock_1_out));
  Register #(.width(32)) register_1 (
    .D(write_data), .en(demultiplexer_1_out0), .clk(clock_1_out), .Q(register_1_q));  // open: clr
  Register #(.width(32)) register_2 (
    .D(write_data), .en(demultiplexer_1_out8), .clk(clock_1_out), .Q(register_2_q));  // open: clr
  Register #(.width(32)) register_3 (
    .D(write_data), .en(demultiplexer_1_out16), .clk(clock_1_out), .Q(register_3_q));  // open: clr
  Register #(.width(32)) register_4 (
    .D(write_data), .en(demultiplexer_1_out24), .clk(clock_1_out), .Q(register_4_q));  // open: clr
  Register #(.width(32)) register_5 (
    .D(write_data), .en(demultiplexer_1_out1), .clk(clock_1_out), .Q(register_5_q));  // open: clr
  Register #(.width(32)) register_6 (
    .D(write_data), .en(demultiplexer_1_out9), .clk(clock_1_out), .Q(register_6_q));  // open: clr
  Register #(.width(32)) register_7 (
    .D(write_data), .en(demultiplexer_1_out17), .clk(clock_1_out), .Q(register_7_q));  // open: clr
  Register #(.width(32)) register_8 (
    .D(write_data), .en(demultiplexer_1_out25), .clk(clock_1_out), .Q(register_8_q));  // open: clr
  Register #(.width(32)) register_9 (
    .D(write_data), .en(demultiplexer_1_out2), .clk(clock_1_out), .Q(register_9_q));  // open: clr
  Register #(.width(32)) register_10 (
    .D(write_data), .en(demultiplexer_1_out10), .clk(clock_1_out), .Q(register_10_q));  // open: clr
  Register #(.width(32)) register_11 (
    .D(write_data), .en(demultiplexer_1_out18), .clk(clock_1_out), .Q(register_11_q));  // open: clr
  Register #(.width(32)) register_12 (
    .D(write_data), .en(demultiplexer_1_out26), .clk(clock_1_out), .Q(register_12_q));  // open: clr
  Register #(.width(32)) register_13 (
    .D(write_data), .en(demultiplexer_1_out3), .clk(clock_1_out), .Q(register_13_q));  // open: clr
  Register #(.width(32)) register_14 (
    .D(write_data), .en(demultiplexer_1_out11), .clk(clock_1_out), .Q(register_14_q));  // open: clr
  Register #(.width(32)) register_15 (
    .D(write_data), .en(demultiplexer_1_out19), .clk(clock_1_out), .Q(register_15_q));  // open: clr
  Register #(.width(32)) register_16 (
    .D(write_data), .en(demultiplexer_1_out27), .clk(clock_1_out), .Q(register_16_q));  // open: clr
  Register #(.width(32)) register_17 (
    .D(write_data), .en(demultiplexer_1_out4), .clk(clock_1_out), .Q(register_17_q));  // open: clr
  Register #(.width(32)) register_18 (
    .D(write_data), .en(demultiplexer_1_out12), .clk(clock_1_out), .Q(register_18_q));  // open: clr
  Register #(.width(32)) register_19 (
    .D(write_data), .en(demultiplexer_1_out20), .clk(clock_1_out), .Q(register_19_q));  // open: clr
  Register #(.width(32)) register_20 (
    .D(write_data), .en(demultiplexer_1_out28), .clk(clock_1_out), .Q(register_20_q));  // open: clr
  Register #(.width(32)) register_21 (
    .D(write_data), .en(demultiplexer_1_out13), .clk(clock_1_out), .Q(register_21_q));  // open: clr
  Register #(.width(32)) register_22 (
    .D(write_data), .en(demultiplexer_1_out21), .clk(clock_1_out), .Q(register_22_q));  // open: clr
  Register #(.width(32)) register_23 (
    .D(write_data), .en(demultiplexer_1_out29), .clk(clock_1_out), .Q(register_23_q));  // open: clr
  Register #(.width(32)) register_24 (
    .D(write_data), .en(demultiplexer_1_out5), .clk(clock_1_out), .Q(register_24_q));  // open: clr
  Register #(.width(32)) register_25 (
    .D(write_data), .en(demultiplexer_1_out14), .clk(clock_1_out), .Q(register_25_q));  // open: clr
  Register #(.width(32)) register_26 (
    .D(write_data), .en(demultiplexer_1_out22), .clk(clock_1_out), .Q(register_26_q));  // open: clr
  Register #(.width(32)) register_27 (
    .D(write_data), .en(demultiplexer_1_out30), .clk(clock_1_out), .Q(register_27_q));  // open: clr
  Register #(.width(32)) register_28 (
    .D(write_data), .en(demultiplexer_1_out6), .clk(clock_1_out), .Q(register_28_q));  // open: clr
  Register #(.width(32)) register_29 (
    .D(write_data), .en(demultiplexer_1_out15), .clk(clock_1_out), .Q(register_29_q));  // open: clr
  Register #(.width(32)) register_30 (
    .D(write_data), .en(demultiplexer_1_out23), .clk(clock_1_out), .Q(register_30_q));  // open: clr
  Register #(.width(32)) register_31 (
    .D(write_data), .en(demultiplexer_1_out31), .clk(clock_1_out), .Q(register_31_q));  // open: clr
  Register #(.width(32)) register_32 (
    .D(write_data), .en(demultiplexer_1_out7), .clk(clock_1_out), .Q(register_32_q));  // open: clr
  Multiplexer #(.select(5), .width(32)) multiplexer_1 (
    .in0(register_1_q), .in1(register_5_q), .in2(register_9_q), .in3(register_13_q), .in4(register_17_q),
    .in5(register_24_q), .in6(register_28_q), .in7(register_32_q), .in8(register_2_q), .in9(register_6_q),
    .in10(register_10_q), .in11(register_14_q), .in12(register_18_q), .in13(register_21_q),
    .in14(register_25_q), .in15(register_29_q), .in16(register_3_q), .in17(register_7_q),
    .in18(register_11_q), .in19(register_15_q), .in20(register_19_q), .in21(register_22_q),
    .in22(register_26_q), .in23(register_30_q), .in24(register_4_q), .in25(register_8_q),
    .in26(register_12_q), .in27(register_16_q), .in28(register_20_q), .in29(register_23_q),
    .in30(register_27_q), .in31(register_31_q), .out(read_data1), .sel(read_reg1));
  Multiplexer #(.select(5), .width(32)) multiplexer_2 (
    .in0(register_1_q), .in1(register_5_q), .in2(register_9_q), .in3(register_13_q), .in4(register_17_q),
    .in5(register_24_q), .in6(register_28_q), .in7(register_32_q), .in8(register_2_q), .in9(register_6_q),
    .in10(register_10_q), .in11(register_14_q), .in12(register_18_q), .in13(register_21_q),
    .in14(register_25_q), .in15(register_29_q), .in16(register_3_q), .in17(register_7_q),
    .in18(register_11_q), .in19(register_15_q), .in20(register_19_q), .in21(register_22_q),
    .in22(register_26_q), .in23(register_30_q), .in24(register_4_q), .in25(register_8_q),
    .in26(register_12_q), .in27(register_16_q), .in28(register_20_q), .in29(register_23_q),
    .in30(register_27_q), .in31(register_31_q), .out(read_data2), .sel(read_reg2));

  // Notes on the sheet:
  //   write_reg: initial=0x1
  //   write_data: initial=0x100
endmodule

module alu (
  input  [31:0] input_a,
  input  [31:0] input_b,
  input  [3:0] alu_op,
  output [31:0] alu_out,
  output c_out
);

  wire [31:0] adder_1_out, and_1_out, or_1_out, subtractor_1_out;

  assign and_1_out = input_a & input_b;  // AND_Gate and_1, 32 bits wide
  assign or_1_out = input_a | input_b;  // OR_Gate or_1, 32 bits wide
  Adder #(.width(32)) adder_1 (.a(input_a), .b(input_b), .out(adder_1_out), .cout(c_out));  // open: cin
  Subtractor #(.width(32)) subtractor_1 (.a(input_a), .b(input_b), .out(subtractor_1_out), .bout(c_out));  // open: bin
  Multiplexer #(.select(4), .width(32)) multiplexer_1 (
    .in0(and_1_out), .in1(or_1_out), .in2(adder_1_out), .in3(subtractor_1_out), .out(alu_out), .sel(alu_op));  // open: in4, in5, in6, in7, in8, in9, in10, in11, in12, in13, in14, in15
endmodule

module main (
);

  wire clock_1_out, clock_2_out;
  wire [1:0] undriven_2;
  wire [4:0] multiplexer_1_out;
  wire [7:0] alu_1_alu_out_2, undriven, undriven_3, undriven_4;
  wire [19:0] PC_q;
  wire [23:0] alu_1_alu_out;
  wire [31:0] adder_1_out, adder_2_out, multiplexer_2_out, multiplexer_3_out, multiplexer_4_out, ram_1_dout,
       registers_1_read_data1, registers_1_read_data2, shifter_1_out;
  wire [31:20] PC_q_2;

  Register #(.width(32)) PC (
    .D(multiplexer_3_out), .clk(clock_1_out), .Q({PC_q_2, PC_q}), .clr(PC_q_2[20]));  // open: en
  Clock clock_1 (.out(clock_1_out));
  // ROM #(.addrWidth(20), .line("quad")) rom_1: pin names not known; wires that end beside it: PC_q, 32'h4
  Adder #(.width(32)) adder_1 (.a({PC_q_2, PC_q}), .b(32'h4), .out(adder_1_out));  // open: cin, cout
  Multiplexer #(.width(5)) multiplexer_1 (
    .in0(undriven[4:0]), .in1(undriven_4[7:3]), .out(multiplexer_1_out));  // open: sel
  registers registers_1 (
    .write_reg(multiplexer_1_out), .read_reg2(undriven[4:0]), .read_reg1({undriven_2, undriven[7:5]}),
    .read_data1(registers_1_read_data1), .read_data2(registers_1_read_data2));  // open: write_data
  Shifter #(.width(32)) shifter_1 (
    .in({{17{undriven_4[7]}}, undriven_4[6:0], undriven_3}), .\dist (5'b00010), .out(shifter_1_out));
  Multiplexer #(.width(32)) multiplexer_2 (
    .in0(registers_1_read_data2), .in1({{17{undriven_4[7]}}, undriven_4[6:0], undriven_3}),
    .out(multiplexer_2_out));  // open: sel
  Adder #(.width(32)) adder_2 (.a(adder_1_out), .b(shifter_1_out), .out(adder_2_out));  // open: cin, cout
  Multiplexer #(.width(32)) multiplexer_3 (.in0(adder_1_out), .in1(adder_2_out), .out(multiplexer_3_out));  // open: sel
  alu alu_1 (
    .input_a(registers_1_read_data1), .input_b(multiplexer_2_out), .alu_out({alu_1_alu_out_2, alu_1_alu_out}));  // open: alu_op, c_out
  Clock clock_2 (.out(clock_2_out));
  RAM #(.addrWidth(24), .dataWidth(32)) ram_1 (
    .addr(alu_1_alu_out), .clk(clock_2_out), .din(registers_1_read_data2), .dout(ram_1_dout));  // open: we, oe
  Multiplexer #(.width(32)) multiplexer_4 (
    .in0(ram_1_dout), .in1({alu_1_alu_out_2, alu_1_alu_out}), .out(multiplexer_4_out));  // open: sel
endmodule
